# Fritzing sketch 171214016_2 (saved by Fritzing 0.9.3b)
breadboards: 1

parts:
  IC2 = MCP3008 8-channel 10-bit ADC [part_number=MCP3008]
  R1 = Resistor [tolerance=±5% resistance=47k package=THT]
  Raspberry_Pi_1 = Raspberry Pi 3 [part_number=RPI-3-V1.2]
  Parça2 = MQ-135

nets:
  N1: IC2.no_name_yet#1, R1.Pin_0, Parça2.AO
  N2: IC2.no_name_yet#10, Raspberry_Pi_1.GPIO8
  N3: IC2.no_name_yet#11, Raspberry_Pi_1.GPIO24
  N4: IC2.no_name_yet#12, Raspberry_Pi_1.GPIO23
  N5: IC2.no_name_yet#13, Raspberry_Pi_1.GPIO18
  GND: IC2.no_name_yet#14, R1.Pin_1, Raspberry_Pi_1.GND, Parça2.GND
  5V: IC2.no_name_yet#15, IC2.no_name_yet#16, Raspberry_Pi_1.5V, Parça2.VCC

custom parts:
  MQ-135: SKU: 101282
